// Logisim project au.circ as structural Verilog: 1 circuit, main circuit ALU
module ALU (
  input  [31:0] reg1,
  input  [31:0] reg2,
  input  [4:0] shiftAmount,
  input  [3:0] operation,
  input  [2:0] branchType,
  output [31:0] result,
  output zero,
  output [1:0] PCcontrol
);

  wire comparator_1_eq, comparator_1_gt, comparator_1_lt, comparator_2_lt, comparator_3_eq, not_1_out,
       or_1_out, or_2_out;
  wire [0:0] comparator_3_lt;
  wire [5:0] FUNC, OP;
  wire [31:0] ADD, ADDu, AND0, BEQ, BGEZ, BGTZ, BLEZ, BNE, DIV, Iformat, LB, LUI, LW, MULT, NOR0, OR0,
       Rformat, SB, shifter_6_out, SLL0, SLLV0, SLT, SRA0, SRL0, SRLV0, SUB, SUBu, SW, SYS, XOR0;

  Comparator #(.width(32)) comparator_1 (
    .a(reg1), .b({32{1'b0}}), .gt(comparator_1_gt), .eq(comparator_1_eq), .lt(comparator_1_lt));
  or or_1 (or_1_out, comparator_1_eq, comparator_1_lt);
  or or_2 (or_2_out, comparator_1_eq, comparator_1_gt);
  Adder #(.width(32)) adder_1 (.a(reg1), .b(reg2), .out(ADD));  // open: cin, cout
  Subtractor #(.width(32)) subtractor_1 (.a(reg1), .b(reg2), .out(SUB));  // open: bin, bout
  assign XOR0 = reg1 ^ reg2;  // XOR_Gate xor_1, 32 bits wide
  assign AND0 = reg1 & reg2;  // AND_Gate and_1, 32 bits wide
  assign OR0 = reg1 | reg2;  // OR_Gate or_3, 32 bits wide
  assign NOR0 = ~(reg1 | reg2);  // NOR_Gate nor_1, 32 bits wide
  Multiplier #(.width(32)) multiplier_1 (.a(reg1), .b(reg2), .out(MULT));  // open: cin, cout
  Divider #(.width(32)) divider_1 (.a(reg1), .b(reg2), .out(DIV));  // open: upper, rem
  Shifter #(.width(32)) shifter_1 (.in(reg2), .\dist (shiftAmount), .out(SLL0));
  Shifter #(.width(32)) shifter_2 (.in(reg2), .\dist (reg1[4:0]), .out(SLLV0));
  Shifter #(.shift("lr"), .width(32)) shifter_3 (.in(reg2), .\dist (shiftAmount), .out(SRL0));
  Shifter #(.shift("lr"), .width(32)) shifter_4 (.in(reg2), .\dist (reg1[4:0]), .out(SRLV0));
  Shifter #(.shift("ar"), .width(32)) shifter_5 (.in(reg2), .\dist (shiftAmount), .out(SRA0));
  Comparator #(.width(32)) comparator_2 (.a(reg1), .b(reg2), .lt(comparator_2_lt));  // open: gt, eq
  Comparator #(.width(32)) comparator_3 (
    .a(reg1), .b(reg2), .eq(comparator_3_eq), .lt(comparator_3_lt[0]));  // open: gt
  Shifter #(.width(32)) shifter_6 (.in(reg2), .\dist (5'b10000), .out(shifter_6_out));
  assign SLT = {{31{1'b0}}, comparator_2_lt};  // Bit_Extender bit_extender_1
  not not_1 (not_1_out, comparator_3_eq);
  Multiplexer #(.select(3)) multiplexer_1 (
    .in1(or_2_out), .in4(comparator_3_eq), .in5(not_1_out), .in6(or_1_out), .in7(comparator_1_gt),
    .out(zero), .sel(branchType));  // open: in0, in2, in3
  Multiplexer #(.select(5), .width(32)) multiplexer_2 (
    .in0(SLL0), .in2(SRL0), .in3(SRA0), .in4(SLLV0), .in6(SRLV0), .in8(MULT), .in10(DIV), .in12(SYS),
    .in16(ADD), .in17(ADDu), .in18(SUB), .in19(SUBu), .in20(AND0), .in21(OR0), .in22(XOR0), .in23(NOR0),
    .in26(SLT), .out(Rformat), .sel({FUNC[5], FUNC[3:0]}));  // open: in1, in5, in7, in9, in11, in13, in14, in15, in24, in25, in27, in28, in29, in30, in31
  Multiplexer #(.select(5), .width(32)) multiplexer_3 (
    .in0(Rformat), .in1(BGEZ), .in4(BEQ), .in5(BNE), .in6(BLEZ), .in7(BGTZ), .in8(ADD), .in9(ADDu),
    .in10(SLT), .in12(AND0), .in13(OR0), .in14(XOR0), .in15(LUI), .in16(LB), .in19(LW), .in24(SB), .in27(SW),
    .out(Iformat), .sel({OP[5], OP[3:0]}));  // open: in2, in3, in11, in17, in18, in20, in21, in22, in23, in25, in26, in28, in29, in30, in31

  // Other names for the same wires on the sheet: PC[1:0] = PCcontrol; SA[4:0] = shiftAmount

  // Notes on the sheet:
  //   inputs
  //   Adder
  //   Unsigned Adder
  //   Subtractor
  //   Unsigned Subtractor
  //   XOR
  //   AND
  //   OR
  //   NOR
  //   Multiplier
  //   Divider
  //   Comprator
  //   000100
  //   000101
  //   000110
  //   000111
  //   000001
  //   001000
  //   001111
  //   101010
  //   001010
endmodule
