// Logisim project cpu.circ as structural Verilog: 1 circuit, main circuit cpu
module cpu (
  input  Start,
  input  Clk
);

  wire adder_1_p1, adder_1_p3, adder_1_p5, adder_2_p2, adder_2_p4, alu_1_p1, alu_1_p2, alu_1_p8,
       alu_control_1_p5, alu_control_1_p6, alu_control_1_p7, alu_control_1_p8, alu_control_1_p9,
       alu_control_1_p10, alu_control_1_p11, DataMem_p1, DataMem_p14, IDCLK, IFCLK, InstMem_2_p9,
       InstMem_2_p10, InstMem_2_p12, InstMem_2_p13, InstMem_2_p14, InstMem_2_p15, InstMem_2_p16,
       InstMem_2_p17, InstMem_p2, InstMem_p3, InstMem_p10, InstMem_p11, InstMem_p12, InstMem_p16,
       InstMem_p17, InstMem_p18, InstMem_p19, InstMem_p20, InstMem_p21, InstMem_p22, InstMem_p23,
       InstMem_p32, isJAL, isRes, isWriteRD, MEMCLK, not_1_p2, PC_p1, PC_p4, RegisterFile_p1,
       RegisterFile_p6, RegisterFile_p7, RegisterFile_p8, RegisterFile_p10, RegisterFile_p11,
       RegisterFile_p13, RegisterFile_p14, RegisterFile_p24, RegisterFile_p27, RegisterFile_p28,
       RegisterFile_p29, syscall, WriteReg, zero;
  wire [1:0] PCcontrol;
  wire [4:0] rd, rs, rt, sa;
  wire [5:0] func, OP;
  wire [31:0] Byte, DataMem_p8, DataMem_p15, imm32, INS, nPC, PC4, res, rsdata, rtdata, shifter_1_out;

  // NOT_Gate not_1: pin names not known; wires that end beside it: syscall, not_1_p2, not_1_p2
  // Register #(.width(32)) PC: pin names not known; wires that end beside it: PC_p1, not_1_p2, nPC, PC_p4
  Shifter #(.width(32)) shifter_1 (.out(shifter_1_out));  // open: in, dist
  // Adder #(.width(32)) adder_1: pin names not known; wires that end beside it: adder_1_p1, adder_1_p1, adder_1_p3, shifter_1_out, adder_1_p5
  // Adder #(.width(32)) adder_2: pin names not known; wires that end beside it: PC_p4, adder_2_p2, 32'h4, adder_2_p4, adder_2_p4, PC4
  // mem InstMem: pin names not known; wires that end beside it: 2'b00, InstMem_p2, InstMem_p3, PC_p4, InstMem_p2, InstMem_p3, 4'b0000, {32{1'b0}}, IFCLK, InstMem_p10, InstMem_p11, InstMem_p12, InstMem_p10, InstMem_p11, InstMem_p12, InstMem_p16, InstMem_p17, InstMem_p18, InstMem_p19, InstMem_p20, InstMem_p21, InstMem_p22, InstMem_p23, InstMem_p16, InstMem_p17, InstMem_p18, InstMem_p19, InstMem_p20, InstMem_p21, InstMem_p22, PCcontrol, InstMem_p32
  Multiplexer #(.select(2), .width(32)) multiplexer_1 ();  // open: in0, in1, in2, in3, out, sel
  // mem InstMem_2: pin names not known; wires that end beside it: InstMem_p32, IFCLK, IDCLK, nPC, INS, rs, rt, {5{1'b1}}, InstMem_2_p9, InstMem_2_p10, rt, InstMem_2_p12, InstMem_2_p13, InstMem_2_p14, InstMem_2_p15, InstMem_2_p16, InstMem_2_p17, isJAL, InstMem_2_p13, InstMem_2_p16
  // Multiplexer #(.width(5)) multiplexer_2: pin names not known; wires that end beside it: rd, isWriteRD
  Multiplexer #(.width(5)) multiplexer_3 ();  // open: in0, in1, out, sel
  Multiplexer #(.width(32)) multiplexer_4 ();  // open: in0, in1, out, sel
  Bit_Extender #(.in_width(16), .out_width(32)) bit_extender_1 ();  // open: in, out
  // ALU_Control alu_control_1: pin names not known; wires that end beside it: InstMem_2_p9, InstMem_2_p10, InstMem_2_p15, InstMem_2_p17, alu_control_1_p5, alu_control_1_p6, alu_control_1_p7, alu_control_1_p8, alu_control_1_p9, alu_control_1_p10, alu_control_1_p11
  // regfile RegisterFile: pin names not known; wires that end beside it: RegisterFile_p1, alu_control_1_p6, alu_control_1_p7, alu_control_1_p8, InstMem_2_p12, RegisterFile_p6, RegisterFile_p7, RegisterFile_p8, RegisterFile_p1, RegisterFile_p10, RegisterFile_p11, rtdata, RegisterFile_p13, RegisterFile_p14, RegisterFile_p13, RegisterFile_p14, rsdata, rtdata, sa, OP, sa, func, OP, RegisterFile_p24, rsdata, func, RegisterFile_p27, RegisterFile_p28, RegisterFile_p29
  // ALU alu_1: pin names not known; wires that end beside it: alu_1_p1, alu_1_p2, RegisterFile_p10, RegisterFile_p11, rsdata, rtdata, imm32, alu_1_p8, RegisterFile_p28, RegisterFile_p29
  // mem DataMem: pin names not known; wires that end beside it: DataMem_p1, RegisterFile_p24, RegisterFile_p27, DataMem_p1, res, zero, PCcontrol, DataMem_p8, isRes, isJAL, isWriteRD, syscall, WriteReg, DataMem_p14, DataMem_p15, res, Byte, rtdata, MEMCLK
  Multiplexer #(.width(32)) multiplexer_5 (.in0(DataMem_p8), .in1(Byte), .out(DataMem_p15), .sel(DataMem_p14));
  // Pins of 4 and 32 bits meet at Byte

  // Notes on the sheet:
  //   PC Control
endmodule
